# Fritzing sketch rtimer (saved by Fritzing 0.7.7b)
perfboards: 1

parts:
  IC1 = IC, DIP package, 8 pins [chip_label=IC]
  J1 = Piezo Speaker
  S1 = Pushbutton [package="[THT]"]
  S2 = Pushbutton [package="[THT]"]
  LED3 = LED - 5mm [color="Red (633nm)" package="5 mm [THT]"]
  LED4 = LED - 5mm [color="Red (633nm)" package="5 mm [THT]"]
  R6 = Resistor [tolerance=±5% resistance=10k package=THT]
  VCC1 = Battery
  C2 = Ceramic Capacitor [capacitance=100nF package="100 mil [THT, multilayer]"]
  LED5 = LED - 5mm [color="Red (633nm)" package="5 mm [THT]"]
  R1 = Resistor [tolerance=±5% resistance=10k package=THT]
  R2 = Resistor [tolerance=±5% resistance=1k package=THT]

nets:
  N1: IC1.pin1, R6.Pin_0, VCC1.+, C2.1, R1.Pin_1
  N2: IC1.pin2, J1.pin2
  N3: IC1.pin3, S1.Pin_3, S1.Pin_4, R1.Pin_0
  N4: IC1.pin4, S2.Pin_3, S2.Pin_4, R6.Pin_1
  N5: IC1.pin5, LED5.anode
  N6: IC1.pin6, LED4.anode
  N7: IC1.pin7, LED3.anode
  N8: IC1.pin8, J1.pin1, S1.Pin_1, S1.Pin_2, S2.Pin_1, S2.Pin_2, VCC1.-, C2.0, R2.Pin_1
  N9: LED3.cathode, LED4.cathode, LED5.cathode, R2.Pin_0
